# Fritzing sketch Sketch (saved by Fritzing 0.9.3b)
breadboards: 1

parts:
  Mod1 = Digispark
  HDMI = IC, SIP package, 20 pins [chip_label=HDMI]
  USBUART1 = PL2303 USB UART Breakout

nets:
  N1: Mod1.VCC, USBUART1.VCCIO
  GND: Mod1.GND, HDMI.pin17, USBUART1.GND
  N2: Mod1.P0, USBUART1.RXD
  N3: Mod1.P2, HDMI.pin13

notes:
  13-CEC
  17-GND

custom parts:
  Digispark: The Digispark is an Attiny85 based microcontroller development board similar to the Arduino line, only cheaper, smaller, and a bit less powerful. With a whole host of shields to extend its functionality and the ability to use the familiar Arduino IDE the Digispark is a great way to jump into electronics, or perfect for when an Arduino is too big or too much. May 2019 modified to correct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
  PL2303 USB UART Breakout: PL2302 Usb Uart Breakout Board with Battery
